# Fritzing sketch Untitled Sketch 2 (saved by Fritzing 0.9.3b)
breadboards: 1

parts:
  hc-sr1 = hc-sr04
  Part1 = Arduino Mega 2560 (Rev3)
  hc-sr2 = hc-sr04
  hc-sr3 = hc-sr04
  hc-sr4 = hc-sr04
  hc-sr5 = hc-sr04
  hc-sr6 = hc-sr04
  hc-sr7 = hc-sr04
  hc-sr8 = hc-sr04
  hc-sr9 = hc-sr04
  hc-sr10 = hc-sr04

nets:
  VCC: hc-sr1.VCC, hc-sr2.VCC, hc-sr3.VCC, hc-sr7.VCC, hc-sr8.VCC
  N1: hc-sr1.Trig, Part1.D22
  N2: hc-sr1.Echo, Part1.D24
  GND: hc-sr1.GND, hc-sr2.GND, hc-sr3.GND, hc-sr7.GND, hc-sr8.GND
  N3: Part1.D26, hc-sr2.Trig
  N4: Part1.D28, hc-sr2.Echo
  N5: Part1.D30, hc-sr3.Trig
  N6: Part1.D32, hc-sr3.Echo
  N7: Part1.D34, hc-sr7.Trig
  N8: Part1.D36, hc-sr7.Echo
  N9: Part1.D38, hc-sr8.Trig
  N10: Part1.D40, hc-sr8.Echo
  VCC_2: hc-sr4.VCC, hc-sr5.VCC, hc-sr6.VCC, hc-sr9.VCC, hc-sr10.VCC
  GND_2: hc-sr4.GND, hc-sr5.GND, hc-sr6.GND, hc-sr9.GND, hc-sr10.GND
