# Fritzing sketch parkirskematik (saved by Fritzing 0.9.3b)
breadboards: 1

parts:
  sensor_B = HC-SR04 Ultrasonic Distance Sensor
  I2C_LCD = LCD1602-I2C
  sensor_C = HC-SR04 Ultrasonic Distance Sensor
  Sensor_Masuk = HC-SR04 Ultrasonic Distance Sensor
  sensor_D = HC-SR04 Ultrasonic Distance Sensor
  sensor_E = HC-SR04 Ultrasonic Distance Sensor
  sesor_F = HC-SR04 Ultrasonic Distance Sensor
  sensor_G = HC-SR04 Ultrasonic Distance Sensor
  sensor_H = HC-SR04 Ultrasonic Distance Sensor
  sensor_I = HC-SR04 Ultrasonic Distance Sensor
  sensor_keluar = HC-SR04 Ultrasonic Distance Sensor
  Raspberry_Pi_1 = Raspberry Pi 3 [part_number=RPI-3-V1.2]
  Arduino_Mega = Arduino Mega 2560 (Rev3)
  servo_masuk = Basic Servo
  sensor_keluar_2 = Basic Servo

nets:
  VCC: sensor_B.VCC, I2C_LCD.VCC, sensor_C.VCC, Sensor_Masuk.VCC, sensor_D.VCC, sensor_E.VCC, sesor_F.VCC, sensor_G.VCC, sensor_H.VCC, sensor_I.VCC, sensor_keluar.VCC, Raspberry_Pi_1.5V, Arduino_Mega.5V, sensor_keluar_2.vcc
  N1: sensor_B.TRIG, Arduino_Mega.D26
  GND: sensor_B.ECHO, sensor_C.ECHO, Sensor_Masuk.ECHO, sensor_D.ECHO, sensor_E.ECHO, Arduino_Mega.GND, sensor_keluar_2.gnd
  N2: sensor_B.GND, Arduino_Mega.D28
  GND_2: I2C_LCD.GND, Raspberry_Pi_1.GND
  N3: I2C_LCD.SDA, Arduino_Mega.D20/SDA, Arduino_Mega.SDA
  N4: I2C_LCD.SCL, Arduino_Mega.D21/SCL
  N5: sensor_C.TRIG, Arduino_Mega.D30
  N6: sensor_C.GND, Arduino_Mega.D32
  N7: Sensor_Masuk.TRIG, Arduino_Mega.D22
  N8: Sensor_Masuk.GND, Arduino_Mega.D24
  N9: sensor_D.TRIG, Arduino_Mega.D34
  N10: sensor_D.GND, Arduino_Mega.D36
  N11: sensor_E.TRIG, Arduino_Mega.D38
  N12: sensor_E.GND, Arduino_Mega.D40
  N13: sesor_F.TRIG, Arduino_Mega.D42
  N14: sesor_F.ECHO, sensor_H.ECHO
  N15: sesor_F.GND, Arduino_Mega.D44
  N16: sensor_G.TRIG, Arduino_Mega.D46
  N17: sensor_G.GND, Arduino_Mega.D48
  N18: sensor_H.TRIG, Arduino_Mega.D50
  N19: sensor_H.GND, Arduino_Mega.D52
  N20: sensor_I.TRIG, Arduino_Mega.D53
  N21: sensor_I.GND, Arduino_Mega.D51
  N22: sensor_keluar.TRIG, Arduino_Mega.D47
  N23: sensor_keluar.GND, Arduino_Mega.D49
  N24: Raspberry_Pi_1.GPIO15, Arduino_Mega.D18/TX1
  N25: Raspberry_Pi_1.GPIO14, Arduino_Mega.D19/RX1
  N26: Arduino_Mega.D2_PWM, sensor_keluar_2.pulse
  N27: Arduino_Mega.D3_PWM, servo_masuk.pulse

custom parts:
  LCD1602-I2C: A standard character display, usually with 2x16 characters. Comes in many colors with LCM1602 IIC attached.
