# Fritzing sketch skematik sensor input (saved by Fritzing 0.9.3b)
breadboards: 1

parts:
  sensor_masuk = hc-sr04
  Arduino_Mega = Arduino Mega 2560 (Rev3)
  ssensor_B = hc-sr04
  sensor_C = hc-sr04
  sensor_F = hc-sr04
  sensor_G = hc-sr04
  sensor_H = hc-sr04
  sensor_D = hc-sr04
  sensor_E = hc-sr04
  sensor_I = hc-sr04
  sesnor_keluar = hc-sr04
  Raspberry_Pi_1 = Raspberry Pi 3 [part_number=RPI-3-V1.2]  # not connected
  I2C_LCD = LCD1602-I2C
  servo_pintu_masuk = Basic Servo
  servo_pintu_keluar = Basic Servo

nets:
  VCC: sensor_masuk.VCC, Arduino_Mega.5V, ssensor_B.VCC, sensor_C.VCC, sensor_F.VCC, sensor_G.VCC, sensor_H.VCC, sensor_D.VCC, sensor_E.VCC, sensor_I.VCC, sesnor_keluar.VCC, I2C_LCD.VCC, servo_pintu_masuk.vcc, servo_pintu_keluar.vcc
  N1: sensor_masuk.Trig, Arduino_Mega.D22
  N2: sensor_masuk.Echo, Arduino_Mega.D24
  GND: sensor_masuk.GND, Arduino_Mega.GND, ssensor_B.GND, sensor_C.GND, sensor_F.GND, sensor_G.GND, sensor_H.GND, sensor_D.GND, sensor_E.GND, sensor_I.GND, sesnor_keluar.GND, servo_pintu_masuk.gnd, servo_pintu_keluar.gnd
  N3: Arduino_Mega.SCL, I2C_LCD.SCL
  N4: Arduino_Mega.SDA, I2C_LCD.SDA
  N5: Arduino_Mega.D3_PWM, servo_pintu_masuk.pulse
  N6: Arduino_Mega.D4_PWM, servo_pintu_keluar.pulse
  N7: Arduino_Mega.D26, ssensor_B.Trig
  N8: Arduino_Mega.D28, ssensor_B.Echo
  N9: Arduino_Mega.D30, sensor_C.Trig
  N10: Arduino_Mega.D32, sensor_C.Echo
  N11: Arduino_Mega.D34, sensor_D.Trig
  N12: Arduino_Mega.D36, sensor_D.Echo
  N13: Arduino_Mega.D38, sensor_E.Trig
  N14: Arduino_Mega.D40, sensor_E.Echo
  N15: Arduino_Mega.D42, sensor_F.Trig
  N16: Arduino_Mega.D44, sensor_F.Echo
  N17: Arduino_Mega.D46, sensor_G.Trig
  N18: Arduino_Mega.D47, sesnor_keluar.Trig
  N19: Arduino_Mega.D48, sensor_G.Echo
  N20: Arduino_Mega.D49, sesnor_keluar.Echo
  N21: Arduino_Mega.D50, sensor_H.Trig
  N22: Arduino_Mega.D51, sensor_I.Echo
  N23: Arduino_Mega.D52, sensor_H.Echo
  N24: Arduino_Mega.D53, sensor_I.Trig

custom parts:
  LCD1602-I2C: A standard character display, usually with 2x16 characters. Comes in many colors with LCM1602 IIC attached.
